# Fritzing sketch main-pcb (saved by Fritzing 0.9.3b)
circuit board: 9.5cm x 7.2cm
breadboards: 1

parts:
  1000μF = Electrolytic Capacitor [capacitance=1000μF voltage=16V package="1010 [SMD, electrolytic]"]
  V1 = DC Power [voltage=5]
  C4 = Capacitor [package=0805]
  C3 = Capacitor [package=0805]
  J2 = Camdenboss CTB0158-3 [part_number=CTB0158-3 package=THT]
  U1 = Voltage Regulator - 5V [package="TO220 [THT]"]
  Part3 = 24 NeoPixel Ring [part_number=1586]
  R5 = Resistor [tolerance=±5% resistance=470 package="0805 [SMD]"]
  Q1 = MOSFET-NCHANNEL [package=sot23-3]
  R3 = Resistor [tolerance=±5% resistance=10k package="0805 [SMD]"]
  R4 = Resistor [tolerance=±5% resistance=10k package="0805 [SMD]"]
  Part4 = Adafruit HUZZAH ESP8266 [part_number="Adafruit #2471"]
  J1 = Screw terminal - 2 pins [package=THT]

nets:
  GND: 1000μF.-, V1.V+, C4.2, C3.2, J2.pin2, U1.GND, Part3.GND, Part4.GND, J1.pin1
  N1: 1000μF.+, V1.V-, C4.1, U1.input_voltage, J1.pin2
  N2: C3.1, J2.pin1, U1.output_voltage, Part3.VDD, R4.Pin_1, Part4.VBAT
  N3: J2.pin3, Part3.IN, R5.Pin_1
  N4: R5.Pin_0, Q1.D, R4.Pin_0
  N5: Q1.G, R3.Pin_0
  N6: Q1.S, Part4.GPIO14
  N7: R3.Pin_1, Part4.3.3V

notes:
  PuckLight
  R0
  Adafruit Huzzah ESP8266
  +5V
  GND
  DATA

custom parts:
  24 NeoPixel Ring: 24 ultra bright smart LED NeoPixels are arranged in a circle with 2.6" (66mm) outer diameter. The rings are 'chainable' - connect the output pin of one to the input pin of another. Use only one microcontroller pin to control as many as you can chain together! Each LED is addressable as the driver chip is inside the LED. Each one has ~18mA constant current drive so the color will be very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
  Adafruit HUZZAH ESP8266: Add Internet to your next project with an adorable, bite-sized WiFi microcontroller, at a price you like! The ESP8266 processor from Espressif is an 80 MHz microcontroller with a full WiFi front-end (both as client and access point) and TCP/IP stack with DNS support as well. While this chip has been very popular, its also been very difficult to use. Most of the low cost modules are not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
